# Fritzing sketch BallPlate (saved by Fritzing 0.8.7b)

parts:
  PWM1 = PCA9685 16x12-bit PWM Breakout
  JACK1 = 2.1mm Barrel Jack with Terminal Block
  Part1 = Arduino Nano (Rev3.0)
  BLUEFRUIT1 = Adafruit Bluefruit EZ-LINK v1.0
  R1 = Resistor [tolerance=±5% resistance=2.2k package=THT]
  R2 = Resistor [tolerance=±5% resistance=4.7k package=THT]
  TouchPanel = Header 4 [package=1x04-smd]
  J1 = Basic Servo
  J2 = Basic Servo
  J3 = Basic Servo

nets:
  N1: PWM1.no_name_yet#0, J1.pulse
  N2: PWM1.no_name_yet#1, J2.pulse
  N3: PWM1.no_name_yet#2, J3.pulse
  N4: PWM1.no_name_yet#100, PWM1.no_name_yet#101, PWM1.no_name_yet#102, PWM1.no_name_yet#706, JACK1.POS
  GND: PWM1.no_name_yet#501, PWM1.no_name_yet#701, PWM1.no_name_yet#1000, PWM1.no_name_yet#1001, PWM1.no_name_yet#1002, JACK1.NEG, Part1.GND, BLUEFRUIT1.GND, R2.Pin_0
  N5: PWM1.no_name_yet#503, Part1.A5
  N6: PWM1.no_name_yet#504, Part1.A4
  5V: PWM1.no_name_yet#505, Part1.5V, BLUEFRUIT1.Vin
  N7: Part1.D1/TX, R1.Pin_0
  N8: Part1.D0/RX, BLUEFRUIT1.TX
  N9: Part1.A3, TouchPanel.4
  N10: Part1.A2, TouchPanel.3
  N11: Part1.A1, TouchPanel.2
  N12: Part1.A0, TouchPanel.1
  N13: BLUEFRUIT1.RX, R1.Pin_1, R2.Pin_1

custom parts:
  Adafruit Bluefruit EZ-LINK v1.0: Bluefruit EZ-LINK, Bluetooth Serial Link & Arduino Programmer
